# Fritzing sketch 12vRelayBoard (saved by Fritzing 0.7.11b)
breadboards: 1

parts:
  Arduino1 = Arduino
  Q1 = NPN-Transistor [part_number=PN2222A package="TO92 [THT]"]
  R1 = Resistor [tolerance=±5% resistance=10k package=THT]
  R2 = Resistor [tolerance=±5% resistance=1k package=THT]
  DIP-Relay1 = DIP-Relay-D31A [part_number=D31A*]
  D1 = Rectifier Diode [package=THT]
  Wifly = Arduino WiFly Shield

nets:
  GND: Arduino1.GND, Q1.E, R2.Pin_1, Wifly.GND
  N1: Arduino1.D9, R1.Pin_0
  N2: Arduino1.D3, Wifly.D3
  N3: Arduino1.D2, Wifly.D2
  3V3: Arduino1.3V3, Wifly.5V
  N4: Arduino1.VIN, DIP-Relay1.COIL1_+, D1.cathode
  N5: Q1.B, R1.Pin_1, R2.Pin_0
  N6: Q1.C, DIP-Relay1.Coil2_-, D1.anode
